# Fritzing sketch sch (saved by Fritzing 0.9.3b)

parts:
  R1 = BBC MicroBit
  S1 = Round Pushbutton
  S2 = Round Pushbutton
  S3 = Round Pushbutton
  R2 = BBC MicroBit
  S4 = Round Pushbutton
  S6 = Round Pushbutton
  LED1 = LED - 5mm [color="White (4500K)" package="5 mm [THT]"]
  R3 = BBC MicroBit
  S7 = Round Pushbutton
  S8 = Round Pushbutton
  S9 = Round Pushbutton

nets:
  N1: R1.GND, S1.leg1, S2.leg1, S3.leg1
  N2: R1.P2_-_ANALOG_IN, S1.leg0
  N3: R1.P1_ANALOG_IN, S2.leg0
  N4: R1.P0_ANALOG_IN, S3.leg0
  N5: R2.GND, S4.leg1, S6.leg1, LED1.cathode
  N6: R2.P2_-_ANALOG_IN, LED1.anode
  N7: R2.P1_ANALOG_IN, S4.leg0
  N8: R2.P0_ANALOG_IN, S6.leg0
  N9: R3.GND, S7.leg1, S8.leg1, S9.leg1
  N10: R3.P2_-_ANALOG_IN, S8.leg0
  N11: R3.P1_ANALOG_IN, S7.leg0
  N12: R3.P0_ANALOG_IN, S9.leg0

notes:
  B button input 'B'
  A button input 'A'
  input '2'
  input '1'
  input '0'
  LED

custom parts:
  BBC MicroBit: The BBC MICRO:BIT
